// Logisim project Lab 3.circ as structural Verilog: 16 circuits, main circuit Main
module Main (
);

  wire Clock, EX_ALU_zero, EX_Ctrl_AluSrc, EX_Ctrl_JAL, ID_BranchIsEqual, ID_Ctrl_ALUOp0, ID_Ctrl_ALUOp1,
       ID_Ctrl_ALUOp2, ID_Ctrl_ALUSrc, ID_Ctrl_Branch, ID_Ctrl_Flush, ID_Ctrl_JAL, ID_Ctrl_Jump,
       ID_Ctrl_JumpReg, ID_Ctrl_MemRead, ID_Ctrl_MemToReg, ID_Ctrl_MemWrite, ID_Ctrl_PCSrc, ID_Ctrl_RegDst,
       ID_Ctrl_RegWrite, ID_Ctrl_Stall, ID_Ctrl_WriteIF_ID, ID_Ctrl_WritePC, M_ALU_zero, M_Ctrl_Branch,
       M_Ctrl_JAL, or_1_out, WB_Ctrl_JAL, WB_Ctrl_MemToReg, WB_Ctrl_RegWrite;
  wire [0:0] EX_Ctrl_EX;
  wire [1:0] EX_Ctrl_ForwardA, EX_Ctrl_ForwardB, EX_Ctrl_WB, ID_Ctrl_ForwardA, ID_Ctrl_ForwardB, M_Ctrl_WB;
  wire [2:0] EX_Ctrl_ALU, EX_Ctrl_AluOp, EX_Ctrl_M, ID_Ctrl_M, ID_Ctrl_WB;
  wire [2:1] M_Ctrl_M;
  wire [4:0] EX_Ins_rd, EX_Ins_rs, EX_Ins_rt, EX_Ins_shamt, EX_WrAddr, ID_Ctrl_EX, M_WrAddr,
       multiplexer_13_out, WB_WrAddr;
  wire [5:0] EX_Ins_func;
  wire [27:0] ID_PC_4;
  wire [31:0] EX_ALU_result, EX_ALUParam_A, EX_ALUParam_B, EX_BranchAddr, EX_FwdData, EX_PC_4, EX_R_rs,
       EX_R_rt, ID_BranchAddr, ID_FwdData_rs, ID_FwdData_rt, ID_Ins, ID_R_rs, ID_R_rt, IF_Ins, IF_NextAddr,
       IF_PC, IF_PC_4, M_ALU_result, M_BranchAddr, M_FwdData, M_PC_4, M_ReadData, multiplexer_1_out,
       multiplexer_2_out, multiplexer_4_out, multiplexer_5_out, multiplexer_11_out, multiplexer_12_out,
       multiplexer_18_out, shifter_1_out, WB_ALU_result, WB_PC_4, WB_ReadData, WB_WrData;
  wire [31:11] EX_SignExtImm;
  wire [31:28] ID_JumpAddr;

  Clock clock_1 (.out(Clock));
  PC pc_1 (.ToPC(IF_NextAddr), .WritePC(ID_Ctrl_WritePC), .Clk(Clock), .PC(IF_PC));
  Instruction_Memory instruction_memory_1 (.PC(IF_PC), .Instruction(IF_Ins));
  Multiplexer #(.width(32), .enable("false")) multiplexer_1 (
    .in0(IF_PC_4), .in1(ID_BranchAddr), .out(multiplexer_1_out), .sel(ID_Ctrl_PCSrc));
  or or_1 (or_1_out, ID_Ctrl_Jump, ID_Ctrl_JAL);
  Multiplexer #(.width(32), .enable("false")) multiplexer_2 (
    .in0(multiplexer_1_out), .in1({ID_JumpAddr, ID_Ins[25:0], 2'b00}), .out(multiplexer_2_out), .sel(or_1_out));
  Adder #(.width(32)) adder_1 (.a(IF_PC), .b(32'h4), .out(IF_PC_4));  // open: cin, cout
  Multiplexer #(.width(32), .enable("false")) multiplexer_3 (
    .in0(multiplexer_2_out), .in1(ID_FwdData_rs), .out(IF_NextAddr), .sel(ID_Ctrl_JumpReg));
  IF_ID IF___ID (
    .PC(IF_PC_4), .Instruction(IF_Ins), .PC_2({ID_JumpAddr, ID_PC_4}), .Instruction_2(ID_Ins), .Clk(Clock),
    .WriteBuffer(ID_Ctrl_WriteIF_ID), .Flush(ID_Ctrl_Flush));
  Multiplexer #(.width(32), .enable("false")) multiplexer_4 (
    .in0(M_ALU_result), .in1(M_PC_4), .out(multiplexer_4_out), .sel(M_Ctrl_JAL));
  Multiplexer #(.width(32), .enable("false")) multiplexer_5 (
    .in0(M_ALU_result), .in1(M_PC_4), .out(multiplexer_5_out), .sel(M_Ctrl_JAL));
  Register_File register_file_1 (
    .WrAddr(WB_WrAddr), .WrData(WB_WrData), .WrReg(WB_Ctrl_RegWrite), .RdAddr1(ID_Ins[25:21]),
    .RdAddr2(ID_Ins[20:16]), .RdData1(ID_R_rs), .RdData2(ID_R_rt), .Clock(Clock));
  Control control_1 (
    .Op31(ID_Ins[31]), .Op30(ID_Ins[30]), .Op29(ID_Ins[29]), .Op28(ID_Ins[28]), .Op27(ID_Ins[27]),
    .Op26(ID_Ins[26]), .RegDst(ID_Ctrl_RegDst), .Jump(ID_Ctrl_Jump), .Branch(ID_Ctrl_Branch),
    .MemRead(ID_Ctrl_MemRead), .MemToReg(ID_Ctrl_MemToReg), .ALUOp0(ID_Ctrl_ALUOp0), .ALUOp1(ID_Ctrl_ALUOp1),
    .ALUOp2(ID_Ctrl_ALUOp2), .MemWrite(ID_Ctrl_MemWrite), .ALUSrc(ID_Ctrl_ALUSrc),
    .RegWrite(ID_Ctrl_RegWrite), .JAL(ID_Ctrl_JAL));
  Hazard_Detection_Unit hazard_detection_unit_1 (
    .EX_Ctrl_M(EX_Ctrl_M), .ID_Ins_rs(ID_Ins[25:21]), .ID_Ins_rt(ID_Ins[20:16]), .EX_WrAddr(EX_WrAddr),
    .ID_Ctrl_WriteIF_ID(ID_Ctrl_WriteIF_ID), .ID_Ctrl_WritePC(ID_Ctrl_WritePC),
    .ID_Ctrl_Stall(ID_Ctrl_Stall), .M_Ctrl_M({M_Ctrl_M, M_Ctrl_Branch}), .ID_Ctrl_Branch(ID_Ctrl_Branch),
    .M_WrAddr(M_WrAddr), .ID_Ctrl_JumpReg(ID_Ctrl_JumpReg), .EX_Ctrl_WB({EX_Ctrl_JAL, EX_Ctrl_WB}));
  Shifter #(.width(32)) shifter_1 (.in({{17{ID_Ins[15]}}, ID_Ins[14:0]}), .\dist (5'b00010), .out(shifter_1_out));
  or or_2 (ID_Ctrl_Flush, ID_Ctrl_Jump, ID_Ctrl_PCSrc, ID_Ctrl_JAL, ID_Ctrl_JumpReg);
  Adder #(.width(32)) adder_2 (.a({ID_JumpAddr, ID_PC_4}), .b(shifter_1_out), .out(ID_BranchAddr));  // open: cin, cout
  and and_1 (ID_Ctrl_PCSrc, ID_Ctrl_Branch, ID_BranchIsEqual);
  Multiplexer #(.select(2), .width(32), .enable("false")) multiplexer_6 (
    .in0(ID_R_rs), .in1(WB_WrData), .in2(multiplexer_4_out), .out(ID_FwdData_rs), .sel(ID_Ctrl_ForwardA));  // open: in3
  Multiplexer #(.select(2), .width(32), .enable("false")) multiplexer_7 (
    .in0(ID_R_rt), .in1(WB_WrData), .in2(multiplexer_5_out), .out(ID_FwdData_rt), .sel(ID_Ctrl_ForwardB));  // open: in3
  Comparator #(.width(32)) comparator_1 (.a(ID_FwdData_rs), .b(ID_FwdData_rt), .eq(ID_BranchIsEqual));  // open: gt, lt
  ALU_Control alu_control_1 (
    .ALUOp2(ID_Ctrl_ALUOp2), .ALUOp1(ID_Ctrl_ALUOp1), .ALUOp0(ID_Ctrl_ALUOp0), .Func5(ID_Ins[5]),
    .Func4(ID_Ins[4]), .Func3(ID_Ins[3]), .Func2(ID_Ins[2]), .Func1(ID_Ins[1]), .Func0(ID_Ins[0]),
    .JumpReg(ID_Ctrl_JumpReg));  // open: ALUControl2, ALUControl1, ALUControl0
  Multiplexer #(.width(5), .enable("false")) multiplexer_8 (
    .in0({ID_Ctrl_ALUSrc, ID_Ctrl_ALUOp2, ID_Ctrl_ALUOp1, ID_Ctrl_ALUOp0, ID_Ctrl_RegDst}), .in1({5{1'b0}}),
    .out(ID_Ctrl_EX), .sel(ID_Ctrl_Stall));
  Multiplexer #(.width(3), .enable("false")) multiplexer_9 (
    .in0({ID_Ctrl_MemWrite, ID_Ctrl_MemRead, ID_Ctrl_Branch}), .in1(3'b000), .out(ID_Ctrl_M),
    .sel(ID_Ctrl_Stall));
  Multiplexer #(.width(3), .enable("false")) multiplexer_10 (
    .in0({ID_Ctrl_JAL, ID_Ctrl_MemToReg, ID_Ctrl_RegWrite}), .in1(3'b000), .out(ID_Ctrl_WB),
    .sel(ID_Ctrl_Stall));
  ID_EX ID___EX (
    .Control_WB(ID_Ctrl_WB), .Control_M(ID_Ctrl_M), .Control_EX(ID_Ctrl_EX), .PC({ID_JumpAddr, ID_PC_4}),
    .R_rs(ID_R_rs), .R_rt(ID_R_rt), .Imm_Sign_Ext({{17{ID_Ins[15]}}, ID_Ins[14:0]}), .Ins_rt(ID_Ins[20:16]),
    .Ins_rd(ID_Ins[15:11]), .Control_WB_2({EX_Ctrl_JAL, EX_Ctrl_WB}), .Control_M_2(EX_Ctrl_M),
    .Control_EX_2({EX_Ctrl_AluSrc, EX_Ctrl_AluOp, EX_Ctrl_EX[0]}), .PC_2(EX_PC_4), .R_rs_2(EX_R_rs),
    .R_rt_2(EX_R_rt), .Imm_Sign_Ext_2({EX_SignExtImm, EX_Ins_shamt, EX_Ins_func}), .Ins_rt_2(EX_Ins_rt),
    .Ins_rd_2(EX_Ins_rd), .Clk(Clock), .Ins_rs(ID_Ins[25:21]), .Ins_rs_2(EX_Ins_rs));
  Multiplexer #(.width(32), .enable("false")) multiplexer_11 (
    .in0(M_ALU_result), .in1(M_PC_4), .out(multiplexer_11_out), .sel(M_Ctrl_JAL));
  Multiplexer #(.width(32), .enable("false")) multiplexer_12 (
    .in0(M_ALU_result), .in1(M_PC_4), .out(multiplexer_12_out), .sel(M_Ctrl_JAL));
  ALU alu_1 (
    .ALUCtl(EX_Ctrl_ALU), .A(EX_ALUParam_A), .B(EX_ALUParam_B), .ALUResult(EX_ALU_result),
    .Zero(EX_ALU_zero), .Shamt(EX_Ins_shamt));  // open: Overflow
  ALU_Control alu_control_2 (
    .ALUOp2(EX_Ctrl_AluOp[2]), .ALUOp1(EX_Ctrl_AluOp[1]), .ALUOp0(EX_Ctrl_AluOp[0]), .Func5(EX_Ins_func[5]),
    .Func4(EX_Ins_func[4]), .Func3(EX_Ins_func[3]), .Func2(EX_Ins_func[2]), .Func1(EX_Ins_func[1]),
    .Func0(EX_Ins_func[0]), .ALUControl2(EX_Ctrl_ALU[2]), .ALUControl1(EX_Ctrl_ALU[1]),
    .ALUControl0(EX_Ctrl_ALU[0]));  // open: JumpReg
  Multiplexer #(.width(5), .enable("false")) multiplexer_13 (
    .in0(EX_Ins_rt), .in1(EX_Ins_rd), .out(multiplexer_13_out), .sel(EX_Ctrl_EX[0]));
  Forwarding_Unit forwarding_unit_1 (
    .EX_Ins_rs(EX_Ins_rs), .EX_Ins_rt(EX_Ins_rt), .M_Ins_rd(M_WrAddr), .WB_Ins_rd(WB_WrAddr),
    .M_Ctrl_WB({M_Ctrl_JAL, M_Ctrl_WB}), .WB_Ctrl_WB({WB_Ctrl_JAL, WB_Ctrl_MemToReg, WB_Ctrl_RegWrite}),
    .EX_Ctrl_ForwardA(EX_Ctrl_ForwardA), .EX_Ctrl_ForwardB(EX_Ctrl_ForwardB),
    .ID_Ctrl_ForwardB(ID_Ctrl_ForwardB), .ID_Ins_rs(ID_Ins[25:21]), .ID_Ins_rt(ID_Ins[20:16]),
    .ID_Ctrl_ForwardA(ID_Ctrl_ForwardA));
  Multiplexer #(.select(2), .width(32), .enable("false")) multiplexer_14 (
    .in0(EX_R_rs), .in1(WB_WrData), .in2(multiplexer_11_out), .out(EX_ALUParam_A), .sel(EX_Ctrl_ForwardA));  // open: in3
  Multiplexer #(.select(2), .width(32), .enable("false")) multiplexer_15 (
    .in0(EX_R_rt), .in1(WB_WrData), .in2(multiplexer_12_out), .out(EX_FwdData), .sel(EX_Ctrl_ForwardB));  // open: in3
  Multiplexer #(.width(5), .enable("false")) multiplexer_16 (
    .in0(multiplexer_13_out), .in1({5{1'b1}}), .out(EX_WrAddr), .sel(EX_Ctrl_JAL));
  EX_MEM EX___MEM (
    .Control_WB({EX_Ctrl_JAL, EX_Ctrl_WB}), .Control_M(EX_Ctrl_M), .Branch_Target(EX_BranchAddr),
    .ALU_zero(EX_ALU_zero), .ALU_Result(EX_ALU_result), .FwdData(EX_FwdData), .Write_Register(EX_WrAddr),
    .Control_WB_2({M_Ctrl_JAL, M_Ctrl_WB}), .Control_M_2({M_Ctrl_M, M_Ctrl_Branch}),
    .Branch_Target_2(M_BranchAddr), .ALU_zero_2(M_ALU_zero), .ALU_Result_2(M_ALU_result),
    .FwdData_2(M_FwdData), .Write_Register_2(M_WrAddr), .Clk(Clock), .PC_4(EX_PC_4), .PC_4_2(M_PC_4));
  Multiplexer #(.width(32), .enable("false")) multiplexer_17 (
    .in0(EX_FwdData), .in1({EX_SignExtImm, EX_Ins_shamt, EX_Ins_func}), .out(EX_ALUParam_B),
    .sel(EX_Ctrl_AluSrc));
  Data_Memory data_memory_1 (
    .MemWrite(M_Ctrl_M[2]), .MemRead(M_Ctrl_M[1]), .WriteAddress(M_ALU_result), .WriteData(M_FwdData),
    .Data_Out(M_ReadData), .Clk(Clock));
  MEM_WB MEM___WB (
    .Control_WB({M_Ctrl_JAL, M_Ctrl_WB}), .Read_Data(M_ReadData), .ALU_Result(M_ALU_result),
    .Write_Register(M_WrAddr), .Control_WB_2({WB_Ctrl_JAL, WB_Ctrl_MemToReg, WB_Ctrl_RegWrite}),
    .Read_Data_2(WB_ReadData), .ALU_Result_2(WB_ALU_result), .Write_Register_2(WB_WrAddr), .Clk(Clock),
    .PC_4(M_PC_4), .PC_4_2(WB_PC_4));
  Multiplexer #(.width(32), .enable("false")) multiplexer_18 (
    .in0(WB_ALU_result), .in1(WB_ReadData), .out(multiplexer_18_out), .sel(WB_Ctrl_MemToReg));
  // Probe on EX_Ctrl_ForwardA
  // Probe on EX_Ctrl_ForwardB
  // Probe on WB_WrData
  // Probe on WB_ALU_result
  // Probe on IF_NextAddr
  // Probe on IF_PC
  // Probe on ID_Ctrl_Branch
  // Probe on ID_Ctrl_Jump
  // Probe on ID_Ctrl_JAL
  // Probe on ID_Ctrl_JumpReg
  // Probe on WB_Ctrl_RegWrite
  // Probe on WB_WrAddr
  // Probe on WB_WrData
  // Probe on M_Ctrl_M[2]
  // Probe on M_FwdData
  Multiplexer #(.width(32), .enable("false")) multiplexer_19 (
    .in0(multiplexer_18_out), .in1(WB_PC_4), .out(WB_WrData), .sel(WB_Ctrl_JAL));

  // Other names for the same wires on the sheet: EX_Ctrl_RegDst = EX_Ctrl_EX[0];
  //   EX_Ctrl_EX[4:1] = {EX_Ctrl_AluSrc, EX_Ctrl_AluOp}; EX_Ctrl_WB[2] = EX_Ctrl_JAL;
  //   EX_SignExtImm[10:0] = {EX_Ins_shamt, EX_Ins_func}; ID_Ins_op[5:0] = ID_Ins[31:26];
  //   ID_Ins_func[5:0] = ID_Ins[5:0]; ID_Ins_imm[15:0] = ID_Ins[15:0]; ID_Ins_jaddress[25:0] = ID_Ins[25:0];
  //   ID_JumpAddr[27:2] = ID_Ins[25:0]; ID_SignExtImm[31:0] = {{17{ID_Ins[15]}}, ID_Ins[14:0]};
  //   ID_Ins_rd[4:0] = ID_Ins[15:11]; ID_Ins_rt[4:0] = ID_Ins[20:16]; ID_Ins_rs[4:0] = ID_Ins[25:21];
  //   ID_PC_4[31:28] = ID_JumpAddr; M_Ctrl_M[0] = M_Ctrl_Branch; M_Ctrl_MemRead = M_Ctrl_M[1];
  //   M_Ctrl_MemWrite = M_Ctrl_M[2]; M_Ctrl_WB[2] = M_Ctrl_JAL;
  //   WB_Ctrl_WB[2:0] = {WB_Ctrl_JAL, WB_Ctrl_MemToReg, WB_Ctrl_RegWrite}

  // Notes on the sheet:
  //   Sign Extender
  //   NAMING CONVENTION: [Phase] Signal [Breakdown]*
  //   For Example: [ID]R[rt] means it is valid for phase ID and it is the value of register rt.
  //   Each column has circuitry for one phase. Forwarding Unit and Hazard Detection have multiple phases.
endmodule

module ALU (
  input  [2:0] ALUCtl,
  input  [31:0] A,
  input  [31:0] B,
  input  [4:0] Shamt,
  output [31:0] ALUResult,
  output Zero,
  output Overflow
);

  wire comparator_1_lt, comparator_2_lt, comparator_3_eq, comparator_4_eq, or_2_out;
  wire [31:0] ADD, AND, NOR, OR, SLL, SLT, SLTU, SRL, SUB, XOR;

  assign XOR = A ^ B;  // XOR_Gate xor_1, 32 bits wide
  Adder #(.width(32)) adder_1 (.a(A), .b(B), .out(ADD));  // open: cin, cout
  Subtractor #(.width(32)) subtractor_1 (.a(A), .b(B), .out(SUB));  // open: bin, bout
  assign AND = A & B;  // AND_Gate and_1, 32 bits wide
  assign OR = A | B;  // OR_Gate or_1, 32 bits wide
  assign NOR = ~(A | B);  // NOR_Gate nor_1, 32 bits wide
  Comparator #(.width(32)) comparator_1 (.a(A), .b(B), .lt(comparator_1_lt));  // open: gt, eq
  assign SLT = {{31{1'b0}}, comparator_1_lt};  // Bit_Extender bit_extender_1
  Shifter #(.width(32)) shifter_1 (.in(B), .\dist (Shamt), .out(SLL));
  Shifter #(.width(32), .shift("lr")) shifter_2 (.in(B), .\dist (Shamt), .out(SRL));
  Comparator #(.width(32), .mode("unsigned")) comparator_2 (.a(A), .b(B), .lt(comparator_2_lt));  // open: gt, eq
  assign SLTU = {{31{1'b0}}, comparator_2_lt};  // Bit_Extender bit_extender_2
  Multiplexer #(.select(3), .width(32), .enable("false")) multiplexer_1 (
    .in0(AND), .in1(ADD), .in2(OR), .in3(SUB), .in4(SLT), .in5(XOR), .in6(SRL), .in7(SLL), .out(ALUResult),
    .sel(ALUCtl));
  Comparator #(.width(3)) comparator_3 (.a(3'b001), .b(ALUCtl), .eq(comparator_3_eq));  // open: gt, lt
  Comparator #(.width(3)) comparator_4 (.a(ALUCtl), .b(3'b011), .eq(comparator_4_eq));  // open: gt, lt
  Overflow_Unit overflow_unit_1 (
    .Add(comparator_3_eq), .Sub(comparator_4_eq), .ASign(A[31]), .BSign(B[31]), .ResultSign(ALUResult[31]),
    .Overflow(Overflow));
  or or_2 (or_2_out, ALUResult[0], ALUResult[1], ALUResult[2], ALUResult[3], ALUResult[4], ALUResult[5], ALUResult[6], ALUResult[7], ALUResult[8], ALUResult[9], ALUResult[10], ALUResult[11], ALUResult[12], ALUResult[13], ALUResult[14], ALUResult[15], ALUResult[16], ALUResult[17], ALUResult[18], ALUResult[19], ALUResult[20], ALUResult[21], ALUResult[22], ALUResult[23], ALUResult[24], ALUResult[25], ALUResult[26], ALUResult[27], ALUResult[28], ALUResult[29], ALUResult[30], ALUResult[31]);
  not not_1 (Zero, or_2_out);

  // Other names for the same wires on the sheet: ASign = A[31]; ResultSign = ALUResult[31]; BSign = B[31]

  // Notes on the sheet:
  //   ALUCtl for ADD on top port
  //   ALUCtl for SUB on second port
endmodule

module Register_File (
  input  [4:0] WrAddr,
  input  [31:0] WrData,
  input  WrReg,
  input  [4:0] RdAddr1,
  input  [4:0] RdAddr2,
  input  Clock,
  output [31:0] RdData1,
  output [31:0] RdData2
);

  wire and_1_out, and_2_out, comparator_1_eq, comparator_2_eq, comparator_3_eq, comparator_4_eq, not_1_out,
       not_2_out, WrReg0, WrReg1, WrReg2, WrReg3, WrReg4, WrReg5, WrReg6, WrReg7, WrReg8, WrReg9, WrReg10,
       WrReg11, WrReg12, WrReg13, WrReg14, WrReg15, WrReg16, WrReg17, WrReg18, WrReg19, WrReg20, WrReg21,
       WrReg22, WrReg23, WrReg24, WrReg25, WrReg26, WrReg27, WrReg28, WrReg29, WrReg30, WrReg31;
  wire [31:0] multiplexer_1_out, multiplexer_2_out, RegData1, RegData2, RegData3, RegData4, RegData5,
       RegData6, RegData7, RegData8, RegData9, RegData10, RegData11, RegData12, RegData13, RegData14,
       RegData15, RegData16, RegData17, RegData18, RegData19, RegData20, RegData21, RegData22, RegData23,
       RegData24, RegData25, RegData26, RegData27, RegData28, RegData29, RegData30, RegData31;

  Demultiplexer #(.select(5), .enable("false")) demultiplexer_1 (
    .out0(WrReg0), .out1(WrReg1), .out2(WrReg2), .out3(WrReg3), .out4(WrReg4), .out5(WrReg5), .out6(WrReg6),
    .out7(WrReg7), .out8(WrReg8), .out9(WrReg9), .out10(WrReg10), .out11(WrReg11), .out12(WrReg12),
    .out13(WrReg13), .out14(WrReg14), .out15(WrReg15), .out16(WrReg16), .out17(WrReg17), .out18(WrReg18),
    .out19(WrReg19), .out20(WrReg20), .out21(WrReg21), .out22(WrReg22), .out23(WrReg23), .out24(WrReg24),
    .out25(WrReg25), .out26(WrReg26), .out27(WrReg27), .out28(WrReg28), .out29(WrReg29), .out30(WrReg30),
    .out31(WrReg31), .in(WrReg), .sel(WrAddr));
  // Probe on RegData4
  Register #(.width(32)) Reg4 (.D(WrData), .en(WrReg4), .Q(RegData4), .clk(Clock));  // open: clr
  // Probe on RegData8
  Register #(.width(32)) Reg8 (.D(WrData), .en(WrReg8), .Q(RegData8), .clk(Clock));  // open: clr
  // Probe on RegData12
  Register #(.width(32)) Reg12 (.D(WrData), .en(WrReg12), .Q(RegData12), .clk(Clock));  // open: clr
  // Probe on RegData16
  Register #(.width(32)) Reg16 (.D(WrData), .en(WrReg16), .Q(RegData16), .clk(Clock));  // open: clr
  // Probe on RegData20
  Register #(.width(32)) Reg20 (.D(WrData), .en(WrReg20), .Q(RegData20), .clk(Clock));  // open: clr
  // Probe on RegData24
  Register #(.width(32)) Reg24 (.D(WrData), .en(WrReg24), .Q(RegData24), .clk(Clock));  // open: clr
  // Probe on RegData28
  Register #(.width(32)) Reg28 (.D(WrData), .en(WrReg28), .Q(RegData28), .clk(Clock));  // open: clr
  Register #(.width(32)) Reg1 (.D(WrData), .en(WrReg1), .Q(RegData1), .clk(Clock));  // open: clr
  Register #(.width(32)) Reg5 (.D(WrData), .en(WrReg5), .Q(RegData5), .clk(Clock));  // open: clr
  Register #(.width(32)) Reg9 (.D(WrData), .en(WrReg9), .Q(RegData9), .clk(Clock));  // open: clr
  Register #(.width(32)) Reg13 (.D(WrData), .en(WrReg13), .Q(RegData13), .clk(Clock));  // open: clr
  Register #(.width(32)) Reg17 (.D(WrData), .en(WrReg17), .Q(RegData17), .clk(Clock));  // open: clr
  Register #(.width(32)) Reg21 (.D(WrData), .en(WrReg21), .Q(RegData21), .clk(Clock));  // open: clr
  Register #(.width(32)) Reg25 (.D(WrData), .en(WrReg25), .Q(RegData25), .clk(Clock));  // open: clr
  Register #(.width(32)) Reg29 (.D(WrData), .en(WrReg29), .Q(RegData29), .clk(Clock));  // open: clr
  // Probe on RegData1
  // Probe on RegData5
  // Probe on RegData9
  // Probe on RegData13
  // Probe on RegData17
  // Probe on RegData21
  // Probe on RegData25
  // Probe on RegData29
  // Probe on RegData2
  Register #(.width(32)) Reg2 (.D(WrData), .en(WrReg2), .Q(RegData2), .clk(Clock));  // open: clr
  // Probe on RegData6
  Register #(.width(32)) Reg6 (.D(WrData), .en(WrReg6), .Q(RegData6), .clk(Clock));  // open: clr
  // Probe on RegData10
  Register #(.width(32)) Reg10 (.D(WrData), .en(WrReg10), .Q(RegData10), .clk(Clock));  // open: clr
  // Probe on RegData14
  Register #(.width(32)) Reg14 (.D(WrData), .en(WrReg14), .Q(RegData14), .clk(Clock));  // open: clr
  // Probe on RegData18
  Register #(.width(32)) Reg18 (.D(WrData), .en(WrReg18), .Q(RegData18), .clk(Clock));  // open: clr
  // Probe on RegData22
  Register #(.width(32)) Reg22 (.D(WrData), .en(WrReg22), .Q(RegData22), .clk(Clock));  // open: clr
  // Probe on RegData26
  Register #(.width(32)) Reg26 (.D(WrData), .en(WrReg26), .Q(RegData26), .clk(Clock));  // open: clr
  // Probe on RegData30
  Register #(.width(32)) Reg30 (.D(WrData), .en(WrReg30), .Q(RegData30), .clk(Clock));  // open: clr
  // Probe on RegData3
  Register #(.width(32)) Reg3 (.D(WrData), .en(WrReg3), .Q(RegData3), .clk(Clock));  // open: clr
  // Probe on RegData7
  Register #(.width(32)) Reg7 (.D(WrData), .en(WrReg7), .Q(RegData7), .clk(Clock));  // open: clr
  // Probe on RegData11
  Register #(.width(32)) Reg11 (.D(WrData), .en(WrReg11), .Q(RegData11), .clk(Clock));  // open: clr
  // Probe on RegData15
  Register #(.width(32)) Reg15 (.D(WrData), .en(WrReg15), .Q(RegData15), .clk(Clock));  // open: clr
  // Probe on RegData19
  Register #(.width(32)) Reg19 (.D(WrData), .en(WrReg19), .Q(RegData19), .clk(Clock));  // open: clr
  // Probe on RegData23
  Register #(.width(32)) Reg23 (.D(WrData), .en(WrReg23), .Q(RegData23), .clk(Clock));  // open: clr
  // Probe on RegData27
  Register #(.width(32)) Reg27 (.D(WrData), .en(WrReg27), .Q(RegData27), .clk(Clock));  // open: clr
  // Probe on RegData31
  Register #(.width(32)) Reg31 (.D(WrData), .en(WrReg31), .Q(RegData31), .clk(Clock));  // open: clr
  Multiplexer #(.select(5), .width(32), .enable("false")) multiplexer_1 (
    .in0({32{1'b0}}), .in1(RegData1), .in2(RegData2), .in3(RegData3), .in4(RegData4), .in5(RegData5),
    .in6(RegData6), .in7(RegData7), .in8(RegData8), .in9(RegData9), .in10(RegData10), .in11(RegData11),
    .in12(RegData12), .in13(RegData13), .in14(RegData14), .in15(RegData15), .in16(RegData16),
    .in17(RegData17), .in18(RegData18), .in19(RegData19), .in20(RegData20), .in21(RegData21),
    .in22(RegData22), .in23(RegData23), .in24(RegData24), .in25(RegData25), .in26(RegData26),
    .in27(RegData27), .in28(RegData28), .in29(RegData29), .in30(RegData30), .in31(RegData31),
    .out(multiplexer_1_out), .sel(RdAddr1));
  Multiplexer #(.select(5), .width(32), .enable("false")) multiplexer_2 (
    .in0({32{1'b0}}), .in1(RegData1), .in2(RegData2), .in3(RegData3), .in4(RegData4), .in5(RegData5),
    .in6(RegData6), .in7(RegData7), .in8(RegData8), .in9(RegData9), .in10(RegData10), .in11(RegData11),
    .in12(RegData12), .in13(RegData13), .in14(RegData14), .in15(RegData15), .in16(RegData16),
    .in17(RegData17), .in18(RegData18), .in19(RegData19), .in20(RegData20), .in21(RegData21),
    .in22(RegData22), .in23(RegData23), .in24(RegData24), .in25(RegData25), .in26(RegData26),
    .in27(RegData27), .in28(RegData28), .in29(RegData29), .in30(RegData30), .in31(RegData31),
    .out(multiplexer_2_out), .sel(RdAddr2));
  Multiplexer #(.width(32), .enable("false")) multiplexer_3 (
    .in0(multiplexer_1_out), .in1(WrData), .out(RdData1), .sel(and_1_out));
  Comparator #(.width(5), .mode("unsigned")) comparator_1 (
    .a(WrAddr), .b(RdAddr2), .eq(comparator_1_eq));  // open: gt, lt
  Multiplexer #(.width(32), .enable("false")) multiplexer_4 (
    .in0(multiplexer_2_out), .in1(WrData), .out(RdData2), .sel(and_2_out));
  Comparator #(.width(5), .mode("unsigned")) comparator_2 (
    .a(WrAddr), .b(RdAddr1), .eq(comparator_2_eq));  // open: gt, lt
  and and_1 (and_1_out, comparator_2_eq, WrReg, not_1_out);
  and and_2 (and_2_out, comparator_1_eq, WrReg, not_2_out);
  Comparator #(.width(5), .mode("unsigned")) comparator_3 (
    .a(WrAddr), .b({5{1'b0}}), .eq(comparator_3_eq));  // open: gt, lt
  not not_1 (not_1_out, comparator_3_eq);
  Comparator #(.width(5), .mode("unsigned")) comparator_4 (
    .a(WrAddr), .b({5{1'b0}}), .eq(comparator_4_eq));  // open: gt, lt
  not not_2 (not_2_out, comparator_4_eq);
endmodule

module Overflow_Unit (
  input  Add,
  input  Sub,
  input  ASign,
  input  BSign,
  input  ResultSign,
  output Overflow
);

  wire and_1_out, and_2_out, or_1_out, xnor_1_out, xor_1_out, xor_2_out;

  xnor xnor_1 (xnor_1_out, ASign, BSign);
  xor xor_1 (xor_1_out, ASign, BSign);
  and and_1 (and_1_out, xnor_1_out, Add);
  and and_2 (and_2_out, xor_1_out, Sub);
  or or_1 (or_1_out, and_1_out, and_2_out);
  xor xor_2 (xor_2_out, ResultSign, ASign);
  and and_3 (Overflow, or_1_out, xor_2_out);

  // Notes on the sheet:
  //   Overflow occurs when doing addition and sign(A) == sign(B) && sign(result) != sign(A)
  //   Or
  //   Overflow occurs when doing subtraction and sign(A) != sign(B) && sign(result) != sign(A)
endmodule

module PC (
  input  WritePC,
  input  [31:0] ToPC,
  input  Clk,
  output [31:0] PC
);

  Register #(.width(32)) register_1 (.D(ToPC), .en(WritePC), .Q(PC), .clk(Clk));  // open: clr
endmodule

module Instruction_Memory (
  input  [31:0] PC,
  output [31:0] Instruction
);

  ROM #(.dataWidth(32)) rom_1 (.addr(PC[9:2]), .data(Instruction));  // open: sel

  // Notes on the sheet:
  //   contents of rom_1 (hex, n*v repeats v):
  //   20010001 5*210820 ac010000 8c020000 211824 ac630000 8c640000 ac640004
endmodule

module Hazard_Detection_Unit (
  input  [4:0] ID_Ins_rs,
  input  [4:0] ID_Ins_rt,
  input  [4:0] EX_WrAddr,
  input  [4:0] M_WrAddr,
  input  ID_Ctrl_Branch,
  input  ID_Ctrl_JumpReg,
  input  [2:0] EX_Ctrl_M,
  input  [2:0] M_Ctrl_M,
  input  [2:0] EX_Ctrl_WB,
  output ID_Ctrl_WriteIF_ID,
  output ID_Ctrl_WritePC,
  output ID_Ctrl_Stall
);

  wire comparator_1_eq, comparator_2_eq, comparator_3_eq, comparator_4_eq, comparator_5_eq, comparator_6_eq,
       comparator_7_eq, comparator_8_eq, comparator_9_eq, EX_WrAddr__0, ID_Ctrl_BranchALUOpStall,
       ID_Ctrl_BranchLdStall, ID_Ctrl_JRALUOpStall, ID_Ctrl_JRLdStall, ID_Ctrl_ReuseStall, or_1_out,
       or_2_out, or_4_out;

  Comparator #(.width(5)) comparator_1 (.a(ID_Ins_rs), .b(EX_WrAddr), .eq(comparator_1_eq));  // open: gt, lt
  Comparator #(.width(5)) comparator_2 (.a(EX_WrAddr), .b(ID_Ins_rt), .eq(comparator_2_eq));  // open: gt, lt
  Comparator #(.width(5)) comparator_3 (.a(EX_WrAddr), .b({5{1'b0}}), .eq(comparator_3_eq));  // open: gt, lt
  Comparator #(.width(5)) comparator_4 (.a(ID_Ins_rs), .b(EX_WrAddr), .eq(comparator_4_eq));  // open: gt, lt
  or or_1 (or_1_out, comparator_1_eq, comparator_2_eq);
  not not_1 (EX_WrAddr__0, comparator_3_eq);
  Comparator #(.width(5)) comparator_5 (.a(ID_Ins_rt), .b(EX_WrAddr), .eq(comparator_5_eq));  // open: gt, lt
  Comparator #(.width(5)) comparator_6 (.a(EX_WrAddr), .b(ID_Ins_rs), .eq(comparator_6_eq));  // open: gt, lt
  and and_1 (ID_Ctrl_BranchALUOpStall, EX_Ctrl_WB[0], ID_Ctrl_Branch, or_1_out, EX_WrAddr__0);
  and and_2 (ID_Ctrl_JRALUOpStall, EX_Ctrl_WB[0], ID_Ctrl_JumpReg, comparator_4_eq, EX_WrAddr__0);
  or or_2 (or_2_out, comparator_5_eq, comparator_6_eq);
  and and_3 (ID_Ctrl_ReuseStall, EX_Ctrl_M[1], or_2_out);
  not not_2 (ID_Ctrl_WriteIF_ID, ID_Ctrl_Stall);
  not not_3 (ID_Ctrl_WritePC, ID_Ctrl_Stall);
  Comparator #(.width(5)) comparator_7 (.a(ID_Ins_rs), .b(M_WrAddr), .eq(comparator_7_eq));  // open: gt, lt
  Comparator #(.width(5)) comparator_8 (.a(M_WrAddr), .b(ID_Ins_rt), .eq(comparator_8_eq));  // open: gt, lt
  Comparator #(.width(5)) comparator_9 (.a(ID_Ins_rs), .b(M_WrAddr), .eq(comparator_9_eq));  // open: gt, lt
  or or_3 (ID_Ctrl_Stall, ID_Ctrl_ReuseStall, ID_Ctrl_BranchALUOpStall, ID_Ctrl_JRALUOpStall, ID_Ctrl_BranchLdStall, ID_Ctrl_JRLdStall);
  or or_4 (or_4_out, comparator_7_eq, comparator_8_eq);
  and and_4 (ID_Ctrl_BranchLdStall, M_Ctrl_M[1], ID_Ctrl_Branch, or_4_out);
  and and_5 (ID_Ctrl_JRLdStall, M_Ctrl_M[1], ID_Ctrl_JumpReg, comparator_9_eq);

  // Other names for the same wires on the sheet: EX_Ctrl_MemRead = EX_Ctrl_M[1]; EX_Ctrl_RegWrite = EX_Ctrl_WB[0];
  //   M_Ctrl_MemRead = M_Ctrl_M[1]
endmodule

module Control (
  input  Op31,
  input  Op30,
  input  Op29,
  input  Op28,
  input  Op27,
  input  Op26,
  output RegDst,
  output Jump,
  output Branch,
  output MemRead,
  output MemToReg,
  output ALUOp0,
  output ALUOp1,
  output ALUOp2,
  output MemWrite,
  output ALUSrc,
  output RegWrite,
  output JAL
);

  wire and_8_out, and_9_out, and_10_out, and_11_out, and_12_out, and_13_out, and_14_out, and_15_out,
       and_16_out, not_1_out, not_2_out, not_3_out, not_4_out, not_5_out, not_6_out, not_7_out, not_8_out,
       not_9_out, not_10_out, not_11_out, not_12_out, not_13_out, not_14_out, not_15_out, not_16_out,
       not_17_out, not_18_out, not_19_out, not_20_out, not_21_out, not_22_out, not_23_out;

  not not_1 (not_1_out, Op29);
  not not_2 (not_2_out, Op27);
  not not_3 (not_3_out, Op31);
  not not_4 (not_4_out, Op29);
  not not_5 (not_5_out, Op29);
  not not_6 (not_6_out, Op29);
  not not_7 (not_7_out, Op31);
  not not_8 (not_8_out, Op27);
  not not_9 (not_9_out, Op30);
  not not_10 (not_10_out, Op29);
  not not_11 (not_11_out, Op30);
  not not_12 (not_12_out, Op28);
  not not_13 (not_13_out, Op30);
  not not_14 (not_14_out, Op28);
  not not_15 (not_15_out, Op28);
  not not_16 (not_16_out, Op27);
  not not_17 (not_17_out, Op27);
  and and_1 (ALUOp2, Op29, Op28);
  and and_2 (MemWrite, Op29, Op27);
  or or_1 (ALUSrc, Op29, Op31);
  not not_18 (not_18_out, Op28);
  not not_19 (not_19_out, Op27);
  not not_20 (not_20_out, Op29);
  not not_21 (not_21_out, Op27);
  not not_22 (not_22_out, Op31);
  not not_23 (not_23_out, Op29);
  and and_3 (RegDst, not_1_out, not_2_out);
  and and_4 (Jump, not_3_out, Op27);
  and and_5 (Branch, not_4_out, Op28);
  and and_6 (MemRead, Op31, not_5_out);
  and and_7 (MemToReg, Op31, not_6_out);
  and and_8 (and_8_out, not_7_out, not_8_out, Op26);
  and and_9 (and_9_out, not_9_out, not_10_out, Op28);
  and and_10 (and_10_out, not_11_out, Op29, not_12_out);
  and and_11 (and_11_out, Op31, not_13_out, not_14_out);
  and and_12 (and_12_out, not_15_out, not_16_out);
  and and_13 (and_13_out, Op30, not_17_out);
  and and_14 (and_14_out, not_18_out, not_19_out);
  and and_15 (and_15_out, not_20_out, Op26);
  and and_16 (and_16_out, Op29, not_21_out);
  and and_17 (JAL, not_22_out, not_23_out, Op26);
  or or_2 (ALUOp0, and_8_out, and_9_out, and_10_out, and_11_out);
  or or_3 (ALUOp1, and_12_out, and_13_out, Op31);
  or or_4 (RegWrite, and_14_out, and_15_out, and_16_out);

  // Notes on the sheet:
  //   Same as Lab 2 (For the first part)
endmodule

module ALU_Control (
  input  ALUOp2,
  input  ALUOp1,
  input  ALUOp0,
  input  Func5,
  input  Func4,
  input  Func3,
  input  Func2,
  input  Func1,
  input  Func0,
  output ALUControl2,
  output ALUControl1,
  output ALUControl0,
  output JumpReg
);

  wire and_1_out, and_2_out, and_3_out, and_4_out, and_5_out, and_6_out, and_7_out, and_8_out, and_9_out,
       and_10_out, not_1_out, not_2_out, not_3_out, not_4_out, not_5_out, not_6_out, not_7_out, not_8_out,
       not_9_out, not_10_out, not_11_out, not_12_out, not_13_out, not_14_out, not_15_out, not_16_out,
       not_17_out, not_18_out, not_19_out, not_20_out, not_21_out, not_22_out, not_23_out, not_24_out,
       not_25_out, not_26_out, not_27_out, not_28_out, not_29_out, not_30_out;

  not not_1 (not_1_out, ALUOp2);
  not not_2 (not_2_out, ALUOp0);
  not not_3 (not_3_out, Func5);
  not not_4 (not_4_out, ALUOp2);
  not not_5 (not_5_out, ALUOp0);
  not not_6 (not_6_out, ALUOp2);
  not not_7 (not_7_out, ALUOp0);
  not not_8 (not_8_out, ALUOp2);
  not not_9 (not_9_out, ALUOp0);
  not not_10 (not_10_out, Func5);
  not not_11 (not_11_out, ALUOp2);
  not not_12 (not_12_out, ALUOp0);
  not not_13 (not_13_out, ALUOp2);
  not not_14 (not_14_out, ALUOp0);
  not not_15 (not_15_out, Func3);
  not not_16 (not_16_out, Func2);
  not not_17 (not_17_out, ALUOp1);
  not not_18 (not_18_out, ALUOp2);
  not not_19 (not_19_out, Func2);
  not not_20 (not_20_out, Func1);
  not not_21 (not_21_out, ALUOp2);
  not not_22 (not_22_out, Func3);
  not not_23 (not_23_out, ALUOp2);
  not not_24 (not_24_out, ALUOp2);
  not not_25 (not_25_out, ALUOp0);
  not not_26 (not_26_out, Func5);
  not not_27 (not_27_out, Func4);
  not not_28 (not_28_out, Func2);
  not not_29 (not_29_out, Func1);
  not not_30 (not_30_out, Func0);
  and and_1 (and_1_out, not_1_out, not_2_out, not_3_out);
  and and_2 (and_2_out, not_4_out, not_5_out, Func2, Func1);
  and and_3 (and_3_out, not_6_out, not_7_out, Func3);
  and and_4 (and_4_out, not_8_out, not_9_out, not_10_out);
  and and_5 (and_5_out, not_11_out, not_12_out, Func0);
  and and_6 (and_6_out, not_13_out, not_14_out, not_15_out, not_16_out, Func1);
  and and_7 (and_7_out, not_17_out, ALUOp0);
  and and_8 (and_8_out, not_18_out, not_19_out, not_20_out);
  and and_9 (and_9_out, not_21_out, Func5, not_22_out, Func1);
  and and_10 (and_10_out, not_23_out, ALUOp0);
  and and_11 (JumpReg, not_24_out, ALUOp1, not_25_out, not_26_out, not_27_out, Func3, not_28_out, not_29_out, not_30_out);
  or or_1 (ALUControl2, and_1_out, and_2_out, and_3_out);
  or or_2 (ALUControl1, and_4_out, and_5_out, and_6_out, and_7_out);
  or or_3 (ALUControl0, and_8_out, and_9_out, and_10_out);

  // Notes on the sheet:
  //   Same as lab 2, except add functionality for SLL and SRL
endmodule

module IF_ID (
  input  Clk,
  input  WriteBuffer,
  input  [31:0] PC,
  input  [31:0] Instruction,
  input  Flush,
  output [31:0] PC_2,
  output [31:0] Instruction_2
);

  wire [31:0] multiplexer_1_out;

  Register #(.width(32)) PC_Buffer (.D(PC), .en(WriteBuffer), .Q(PC_2), .clk(Clk));  // open: clr
  Multiplexer #(.width(32), .enable("false")) multiplexer_1 (
    .in0(Instruction), .in1({32{1'b0}}), .out(multiplexer_1_out), .sel(Flush));
  Register #(.width(32)) Instruction_Buffer (
    .D(multiplexer_1_out), .en(WriteBuffer), .Q(Instruction_2), .clk(Clk));  // open: clr
endmodule

module ID_EX (
  input  [2:0] Control_WB,
  input  Clk,
  input  [2:0] Control_M,
  input  [4:0] Control_EX,
  input  [31:0] PC,
  input  [31:0] R_rs,
  input  [31:0] R_rt,
  input  [31:0] Imm_Sign_Ext,
  input  [4:0] Ins_rs,
  input  [4:0] Ins_rt,
  input  [4:0] Ins_rd,
  output [2:0] Control_WB_2,
  output [2:0] Control_M_2,
  output [4:0] Control_EX_2,
  output [31:0] PC_2,
  output [31:0] R_rs_2,
  output [31:0] R_rt_2,
  output [31:0] Imm_Sign_Ext_2,
  output [4:0] Ins_rs_2,
  output [4:0] Ins_rt_2,
  output [4:0] Ins_rd_2
);

  Register #(.width(3)) Control_WB__Buffer (.D(Control_WB), .Q(Control_WB_2), .clk(Clk));  // open: en, clr
  Register #(.width(3)) Control_M__Buffer (.D(Control_M), .Q(Control_M_2), .clk(Clk));  // open: en, clr
  Register #(.width(5)) Control_EX__Buffer (.D(Control_EX), .Q(Control_EX_2), .clk(Clk));  // open: en, clr
  Register #(.width(32)) PC_Buffer (.D(PC), .Q(PC_2), .clk(Clk));  // open: en, clr
  Register #(.width(32)) R_rs__Buffer (.D(R_rs), .Q(R_rs_2), .clk(Clk));  // open: en, clr
  Register #(.width(32)) R_rt__Buffer (.D(R_rt), .Q(R_rt_2), .clk(Clk));  // open: en, clr
  Register #(.width(32)) ISE_Buffer (.D(Imm_Sign_Ext), .Q(Imm_Sign_Ext_2), .clk(Clk));  // open: en, clr
  Register #(.width(5)) Ins_rs__Buffer (.D(Ins_rs), .Q(Ins_rs_2), .clk(Clk));  // open: en, clr
  Register #(.width(5)) Ins_rt__Buffer (.D(Ins_rt), .Q(Ins_rt_2), .clk(Clk));  // open: en, clr
  Register #(.width(5)) Ins_rd__Buffer (.D(Ins_rd), .Q(Ins_rd_2), .clk(Clk));  // open: en, clr
endmodule

module EX_MEM (
  input  [2:0] Control_WB,
  input  Clk,
  input  [2:0] Control_M,
  input  [31:0] Branch_Target,
  input  ALU_zero,
  input  [31:0] ALU_Result,
  input  [31:0] FwdData,
  input  [4:0] Write_Register,
  input  [31:0] PC_4,
  output [2:0] Control_WB_2,
  output [2:0] Control_M_2,
  output [31:0] Branch_Target_2,
  output ALU_zero_2,
  output [31:0] ALU_Result_2,
  output [31:0] FwdData_2,
  output [4:0] Write_Register_2,
  output [31:0] PC_4_2
);

  Register #(.width(3)) u_Control_WB (.D(Control_WB), .Q(Control_WB_2), .clk(Clk));  // open: en, clr
  Register #(.width(3)) Control_M__Buffer (.D(Control_M), .Q(Control_M_2), .clk(Clk));  // open: en, clr
  Register #(.width(32)) BT_Buffer (.D(Branch_Target), .Q(Branch_Target_2), .clk(Clk));  // open: en, clr
  Register #(.width(1)) ALU_zero__Buffer (.D(ALU_zero), .Q(ALU_zero_2), .clk(Clk));  // open: en, clr
  Register #(.width(32)) ALU_res__Buffer (.D(ALU_Result), .Q(ALU_Result_2), .clk(Clk));  // open: en, clr
  Register #(.width(32)) FwdData_Buffer (.D(FwdData), .Q(FwdData_2), .clk(Clk));  // open: en, clr
  Register #(.width(5)) Write_Register_Buffer (.D(Write_Register), .Q(Write_Register_2), .clk(Clk));  // open: en, clr
  Register #(.width(32)) u_PC_4 (.D(PC_4), .Q(PC_4_2), .clk(Clk));  // open: en, clr
endmodule

module MEM_WB (
  input  [2:0] Control_WB,
  input  Clk,
  input  [31:0] Read_Data,
  input  [31:0] ALU_Result,
  input  [4:0] Write_Register,
  input  [31:0] PC_4,
  output [2:0] Control_WB_2,
  output [31:0] Read_Data_2,
  output [31:0] ALU_Result_2,
  output [4:0] Write_Register_2,
  output [31:0] PC_4_2
);

  Register #(.width(3)) Control_WB__Buffer (.D(Control_WB), .Q(Control_WB_2), .clk(Clk));  // open: en, clr
  Register #(.width(32)) RD_Buffer (.D(Read_Data), .Q(Read_Data_2), .clk(Clk));  // open: en, clr
  Register #(.width(32)) ALU_res__Buffer (.D(ALU_Result), .Q(ALU_Result_2), .clk(Clk));  // open: en, clr
  Register #(.width(5)) Write_Register_Buffer (.D(Write_Register), .Q(Write_Register_2), .clk(Clk));  // open: en, clr
  Register #(.width(32)) u_PC_4 (.D(PC_4), .Q(PC_4_2), .clk(Clk));  // open: en, clr
endmodule

module Data_Memory (
  input  Clk,
  input  MemWrite,
  input  MemRead,
  input  [31:0] WriteAddress,
  input  [31:0] WriteData,
  output [31:0] Data_Out
);

  RAM #(.dataWidth(32), .bus("separate")) ram_1 (
    .addr(WriteAddress[7:0]), .din(WriteData), .data(Data_Out), .str(MemWrite), .clk(Clk), .ld(MemRead));  // open: sel, clr

  // Other names for the same wires on the sheet: WR_Address[31:0] = WriteAddress; WR_Data[31:0] = WriteData
endmodule

module Forwarding_Unit (
  input  [4:0] ID_Ins_rs,
  input  [4:0] ID_Ins_rt,
  input  [4:0] EX_Ins_rs,
  input  [4:0] EX_Ins_rt,
  input  [4:0] M_Ins_rd,
  input  [4:0] WB_Ins_rd,
  input  [2:0] M_Ctrl_WB,
  input  [2:0] WB_Ctrl_WB,
  output [1:0] EX_Ctrl_ForwardA,
  output [1:0] EX_Ctrl_ForwardB,
  output [1:0] ID_Ctrl_ForwardA,
  output [1:0] ID_Ctrl_ForwardB
);

  wire comparator_2_eq, comparator_4_eq, EX_ForwardA_01, EX_ForwardA_10, EX_ForwardB_01, EX_ForwardB_10,
       ID_ForwardA_01, ID_ForwardA_10, ID_ForwardB_01, ID_ForwardB_10, M_Ins_rd___EX_Ins_rs,
       M_Ins_rd___EX_Ins_rt, M_Ins_rd___ID_Ins_rs, M_Ins_rd___ID_Ins_rt, M_Ins_rd_neq0,
       WB_Ins_rd___EX_Ins_rs, WB_Ins_rd___EX_Ins_rt, WB_Ins_rd___ID_Ins_rs, WB_Ins_rd___ID_Ins_rt,
       WB_Ins_rd_neq0;

  Comparator #(.width(5)) comparator_1 (.a(EX_Ins_rs), .b(M_Ins_rd), .eq(M_Ins_rd___EX_Ins_rs));  // open: gt, lt
  Comparator #(.width(5)) comparator_2 (.a(M_Ins_rd), .b({5{1'b0}}), .eq(comparator_2_eq));  // open: gt, lt
  not not_1 (M_Ins_rd_neq0, comparator_2_eq);
  Comparator #(.width(5)) comparator_3 (.a(EX_Ins_rs), .b(WB_Ins_rd), .eq(WB_Ins_rd___EX_Ins_rs));  // open: gt, lt
  Comparator #(.width(5)) comparator_4 (.a(WB_Ins_rd), .b({5{1'b0}}), .eq(comparator_4_eq));  // open: gt, lt
  not not_2 (WB_Ins_rd_neq0, comparator_4_eq);
  Comparator #(.width(5)) comparator_5 (.a(ID_Ins_rs), .b(M_Ins_rd), .eq(M_Ins_rd___ID_Ins_rs));  // open: gt, lt
  Comparator #(.width(5)) comparator_6 (.a(ID_Ins_rs), .b(WB_Ins_rd), .eq(WB_Ins_rd___ID_Ins_rs));  // open: gt, lt
  and and_1 (ID_ForwardA_10, M_Ctrl_WB[0], M_Ins_rd_neq0, M_Ins_rd___ID_Ins_rs);
  and and_2 (ID_ForwardB_10, M_Ctrl_WB[0], M_Ins_rd_neq0, M_Ins_rd___ID_Ins_rt);
  and and_3 (EX_ForwardA_10, M_Ctrl_WB[0], M_Ins_rd___EX_Ins_rs, M_Ins_rd_neq0);
  and and_4 (EX_ForwardB_10, M_Ctrl_WB[0], M_Ins_rd___EX_Ins_rt, M_Ins_rd_neq0);
  and and_5 (EX_ForwardA_01, WB_Ctrl_WB[0], WB_Ins_rd_neq0, ~EX_ForwardA_10, WB_Ins_rd___EX_Ins_rs);  // AND_Gate
  and and_6 (EX_ForwardB_01, WB_Ctrl_WB[0], WB_Ins_rd_neq0, ~EX_ForwardB_10, WB_Ins_rd___EX_Ins_rt);  // AND_Gate
  Comparator #(.width(5)) comparator_7 (.a(EX_Ins_rt), .b(M_Ins_rd), .eq(M_Ins_rd___EX_Ins_rt));  // open: gt, lt
  Comparator #(.width(5)) comparator_8 (.a(EX_Ins_rt), .b(WB_Ins_rd), .eq(WB_Ins_rd___EX_Ins_rt));  // open: gt, lt
  Comparator #(.width(5)) comparator_9 (.a(ID_Ins_rt), .b(M_Ins_rd), .eq(M_Ins_rd___ID_Ins_rt));  // open: gt, lt
  Comparator #(.width(5)) comparator_10 (.a(ID_Ins_rt), .b(WB_Ins_rd), .eq(WB_Ins_rd___ID_Ins_rt));  // open: gt, lt
  and and_7 (ID_ForwardA_01, WB_Ctrl_WB[0], WB_Ins_rd_neq0, ~ID_ForwardA_10, WB_Ins_rd___ID_Ins_rs);  // AND_Gate
  and and_8 (ID_ForwardB_01, WB_Ctrl_WB[0], WB_Ins_rd_neq0, ~ID_ForwardB_10, WB_Ins_rd___ID_Ins_rt);  // AND_Gate
  ForwardSimplifier2 forwardsimplifier2_1 (
    .A01(EX_ForwardA_01), .A10(EX_ForwardA_10), .Out1(EX_Ctrl_ForwardA[1]), .Out0(EX_Ctrl_ForwardA[0]));
  ForwardSimplifier2 forwardsimplifier2_2 (
    .A01(EX_ForwardB_01), .A10(EX_ForwardB_10), .Out1(EX_Ctrl_ForwardB[1]), .Out0(EX_Ctrl_ForwardB[0]));
  ForwardSimplifier2 forwardsimplifier2_3 (
    .A01(ID_ForwardA_01), .A10(ID_ForwardA_10), .Out1(ID_Ctrl_ForwardA[1]), .Out0(ID_Ctrl_ForwardA[0]));
  ForwardSimplifier2 forwardsimplifier2_4 (
    .A01(ID_ForwardB_01), .A10(ID_ForwardB_10), .Out1(ID_Ctrl_ForwardB[1]), .Out0(ID_Ctrl_ForwardB[0]));

  // Other names for the same wires on the sheet: M_Ctrl_RegWrite = M_Ctrl_WB[0]; WB_Ctrl_RegWrite = WB_Ctrl_WB[0]

  // Notes on the sheet:
  //   [ID]: Control Forwarding
endmodule

module ForwardSimplifier2 (
  input  A01,
  input  A10,
  output Out1,
  output Out0
);

  wire not_1_out, not_2_out;

  not not_1 (not_1_out, A01);
  not not_2 (not_2_out, A10);
  and and_1 (Out1, not_1_out, A10);
  and and_2 (Out0, A01, not_2_out);
endmodule
