// Logisim project Lab3_db.circ as structural Verilog: 9 circuits, main circuit Main
module Main (
);

  wire ALUSrc, and_1_out, Branch, Clock, EX_MEM_Branch, EX_MEM_MemRead, EX_MEM_MemtoReg, EX_MEM_MemWrite,
       EX_MEM_Pass_Zero, EX_MEM_RegWrite, ID_EX_ALUSrc, ID_EX_Branch, ID_EX_MemRead, ID_EX_MemtoReg,
       ID_EX_MemWrite, ID_EX_RegDst, ID_EX_RegWrite, Jal, Jr, Jump, MEM_WB_MemtoReg, MEM_WB_WrReg, MemRead,
       MemtoReg, MemWr, RegDst, Zero_into_EX_MEM;
  wire [1:0] ALUOp, ID_EX_ALUOp;
  wire [2:0] ALUCtl;
  wire [4:0] multiplexer_1_out, WrAddr;
  wire [5:0] func;
  wire [31:0] Adder_Result_into_EX_MEM, ALU_Result_into_MEM_EX, ALUResult_into_EX_MEM,
       EX_MEM_Pass_Adder_Result, EX_MEM_Pass_RdData2, ID_EX_Pass_ImmExtended, ID_EX_Pass_PC_4,
       ID_EX_Pass_RdData1, ID_EX_Pass_RdData2, IF_ID_Pass_PC_4, ImmExtended_Into_ID_EX, InstrMem_Into_IF_ID,
       MEM_WB_Pass_ALU_Result, MEM_WB_Pass_RdData, multiplexer_3_out, multiplexer_4_out, multiplexer_5_out,
       multiplexer_7_out, PC_4_Into_IF_ID, PC_prime, RdData1_Into_ID_EX, RdData2_Into_ID_EX,
       RdData_into_MEM_EX, register_1_q, shifter_1_out, WrData;
  wire [31:6] IF_ID_Pass_InstrMem;

  Clock clock_1 (.out(Clock));
  Register #(.width(32)) register_1 (.D(PC_prime), .Q(register_1_q), .clk(Clock));  // open: en, clr
  IF_ID IF_ID (
    .Clock(Clock), .in_2(PC_4_Into_IF_ID), .in_3(InstrMem_Into_IF_ID), .out_4(IF_ID_Pass_PC_4),
    .out_5({IF_ID_Pass_InstrMem, func}));
  Adder #(.width(32)) adder_1 (.a(32'h4), .b(register_1_q), .out(PC_4_Into_IF_ID));  // open: cin, cout
  ROM #(.dataWidth(32)) rom_1 (.addr(register_1_q[9:2]), .data(InstrMem_Into_IF_ID));  // open: sel
  Multiplexer #(.width(5), .enable("false")) multiplexer_1 (
    .in0(IF_ID_Pass_InstrMem[20:16]), .in1(IF_ID_Pass_InstrMem[15:11]), .out(multiplexer_1_out),
    .sel(ID_EX_RegDst));
  Multiplexer #(.width(5), .enable("false")) multiplexer_2 (
    .in0(multiplexer_1_out), .in1({5{1'b1}}), .out(WrAddr), .sel(Jal));
  Control_Unit control_unit_1 (
    .opcode(IF_ID_Pass_InstrMem[31:26]), .func(func), .ALUSrc(ALUSrc), .Branch(Branch), .Jal(Jal), .Jr(Jr),
    .Jump(Jump), .MemRead(MemRead), .MemtoReg(MemtoReg), .MemWr(MemWr), .RegDst(RegDst), .WrReg(MemtoReg),
    .ALUCtl(ALUCtl));
  Register_File register_file_1 (
    .WrAddr(WrAddr), .WrData(WrData), .WrReg(MEM_WB_WrReg), .RdAddr1(IF_ID_Pass_InstrMem[25:21]),
    .RdAddr2(IF_ID_Pass_InstrMem[20:16]), .RdData1(RdData1_Into_ID_EX), .RdData2(RdData2_Into_ID_EX),
    .Clock(Clock));
  assign ImmExtended_Into_ID_EX = {{16{IF_ID_Pass_InstrMem[15]}}, {IF_ID_Pass_InstrMem[15:6], func}};  // Bit_Extender bit_extender_1
  ID_EX ID_EX (
    .Clock(Clock), .in_2(MemtoReg), .in_3(MemtoReg), .in_4(MemRead), .in_5(MemWr), .in_6(RegDst),
    .in_7(ALUOp), .in_8(ALUSrc), .in_9(Branch), .in_10(IF_ID_Pass_PC_4), .in_11(RdData1_Into_ID_EX),
    .in_12(RdData2_Into_ID_EX), .in_13(ImmExtended_Into_ID_EX), .out_14(ID_EX_RegWrite),
    .out_15(ID_EX_MemtoReg), .out_16(ID_EX_MemRead), .out_17(ID_EX_MemWrite), .out_18(ID_EX_RegDst),
    .out_19(ID_EX_ALUOp), .out_20(ID_EX_ALUSrc), .out_21(ID_EX_Branch), .out_22(ID_EX_Pass_PC_4),
    .out_23(ID_EX_Pass_RdData1), .out_24(ID_EX_Pass_RdData2), .out_25(ID_EX_Pass_ImmExtended));
  Multiplexer #(.width(32), .enable("false")) multiplexer_3 (
    .in0(EX_MEM_Pass_RdData2), .in1(ID_EX_Pass_ImmExtended), .out(multiplexer_3_out), .sel(ID_EX_ALUSrc));
  Adder #(.width(32)) adder_2 (
    .a(ID_EX_Pass_PC_4), .b(shifter_1_out), .out(Adder_Result_into_EX_MEM));  // open: cin, cout
  Shifter #(.width(32)) shifter_1 (.in(ID_EX_Pass_ImmExtended), .\dist (5'b00010), .out(shifter_1_out));
  ALU alu_1 (
    .ALUCtl(ALUCtl), .A(ID_EX_Pass_RdData1), .B(multiplexer_3_out), .ALUResult(ALUResult_into_EX_MEM),
    .Zero(Zero_into_EX_MEM), .Shamt({5{1'b0}}));  // open: Overflow
  and and_1 (and_1_out, EX_MEM_Branch, EX_MEM_Pass_Zero);
  Multiplexer #(.width(32), .enable("false")) multiplexer_4 (
    .in0(ID_EX_Pass_PC_4), .in1(EX_MEM_Pass_Adder_Result), .out(multiplexer_4_out), .sel(and_1_out));
  Multiplexer #(.width(32), .enable("false")) multiplexer_5 (
    .in0(multiplexer_4_out), .in1({IF_ID_Pass_PC_4[31:28], IF_ID_Pass_InstrMem[25:6], func, 2'b00}),
    .out(multiplexer_5_out), .sel(Jump));
  RAM #(.dataWidth(32), .bus("separate")) ram_1 (
    .addr(ALU_Result_into_MEM_EX[9:2]), .din(EX_MEM_Pass_RdData2), .data(RdData_into_MEM_EX),
    .str(EX_MEM_MemWrite), .clk(Clock), .ld(EX_MEM_MemRead));  // open: sel, clr
  EX_MEM EX_MEM (
    .Clock(Clock), .in_2(ID_EX_Branch), .in_3(ID_EX_RegWrite), .in_4(ID_EX_MemtoReg), .in_5(ID_EX_MemRead),
    .in_6(ID_EX_MemWrite), .in_7(Adder_Result_into_EX_MEM), .Zero(Zero_into_EX_MEM),
    .in_9(ALUResult_into_EX_MEM), .in_10(ID_EX_Pass_RdData2), .out_11(EX_MEM_Branch),
    .out_12(EX_MEM_RegWrite), .out_13(EX_MEM_MemtoReg), .out_14(EX_MEM_MemRead), .out_15(EX_MEM_MemWrite),
    .out_16(EX_MEM_Pass_Adder_Result), .out_17(EX_MEM_Pass_Zero), .out_18(ALU_Result_into_MEM_EX),
    .out_19(EX_MEM_Pass_RdData2));
  Multiplexer #(.width(32), .enable("false")) multiplexer_6 (
    .in0(multiplexer_5_out), .in1(ID_EX_Pass_RdData1), .out(PC_prime), .sel(Jr));
  Multiplexer #(.width(32), .enable("false")) multiplexer_7 (
    .in0(MEM_WB_Pass_ALU_Result), .in1(MEM_WB_Pass_RdData), .out(multiplexer_7_out), .sel(MEM_WB_MemtoReg));
  Multiplexer #(.width(32), .enable("false")) multiplexer_8 (
    .in0(multiplexer_7_out), .in1(IF_ID_Pass_PC_4), .out(WrData), .sel(Jal));
  MEM_WB MEM_WB (
    .Clock(Clock), .in_2(EX_MEM_RegWrite), .in_3(EX_MEM_MemtoReg), .in_4(ALU_Result_into_MEM_EX),
    .in_5(RdData_into_MEM_EX), .out_6(MEM_WB_WrReg), .out_7(MEM_WB_MemtoReg), .out_8(MEM_WB_Pass_RdData),
    .out_9(MEM_WB_Pass_ALU_Result));

  // Other names for the same wires on the sheet: EX_MEM_Pass_ALUResult[31:0] = ALU_Result_into_MEM_EX;
  //   opcode[5:0] = IF_ID_Pass_InstrMem[31:26]; IF_ID_Pass_InstrMem[5:0] = func;
  //   Jump_Address[31:2] = {IF_ID_Pass_PC_4[31:28], IF_ID_Pass_InstrMem[25:6], func};
  //   PC_4_Into_ID_EX[31:0] = IF_ID_Pass_PC_4; PC___4[31:0] = IF_ID_Pass_PC_4; JumpFromReg[31:0] = ID_EX_Pass_RdData1;
  //   RdData2_into_EX_MEM[31:0] = ID_EX_Pass_RdData2; WrReg = MemtoReg

  // Notes on the sheet:
  //   contents of rom_1 (hex, n*v repeats v):
  //   20010008 34220005 3043ffff 612020 832822 223024 c33826 aca40064 8ca80064 22482a 1265025 c00000d
  //   200b0001 23ff0018 10c00003 a13022 800000e 200c0001 3e00008 200d0001 200e0001
endmodule

module ALU (
  input  [2:0] ALUCtl,
  input  [31:0] A,
  input  [31:0] B,
  input  [4:0] Shamt,
  output [31:0] ALUResult,
  output Zero,
  output Overflow
);

  wire comparator_1_lt, comparator_2_lt, comparator_3_eq, comparator_4_eq, or_2_out;
  wire [31:0] ADD, AND, NOR, OR, SLL, SLT, SLTU, SRL, SUB, XOR;

  assign XOR = A ^ B;  // XOR_Gate xor_1, 32 bits wide
  Adder #(.width(32)) adder_1 (.a(A), .b(B), .out(ADD));  // open: cin, cout
  Subtractor #(.width(32)) subtractor_1 (.a(A), .b(B), .out(SUB));  // open: bin, bout
  assign AND = A & B;  // AND_Gate and_1, 32 bits wide
  assign OR = A | B;  // OR_Gate or_1, 32 bits wide
  assign NOR = ~(A | B);  // NOR_Gate nor_1, 32 bits wide
  Comparator #(.width(32)) comparator_1 (.a(A), .b(B), .lt(comparator_1_lt));  // open: gt, eq
  assign SLT = {{31{1'b0}}, comparator_1_lt};  // Bit_Extender bit_extender_1
  Shifter #(.width(32)) shifter_1 (.in(B), .\dist (Shamt), .out(SLL));
  Shifter #(.width(32), .shift("lr")) shifter_2 (.in(B), .\dist (Shamt), .out(SRL));
  Comparator #(.width(32), .mode("unsigned")) comparator_2 (.a(A), .b(B), .lt(comparator_2_lt));  // open: gt, eq
  assign SLTU = {{31{1'b0}}, comparator_2_lt};  // Bit_Extender bit_extender_2
  Multiplexer #(.select(3), .width(32), .enable("false")) multiplexer_1 (
    .in0(AND), .in1(ADD), .in2(OR), .in3(SUB), .in4(SLT), .in5(XOR), .in6(SRL), .in7(SLL), .out(ALUResult),
    .sel(ALUCtl));
  Comparator #(.width(3)) comparator_3 (.a(3'b001), .b(ALUCtl), .eq(comparator_3_eq));  // open: gt, lt
  Comparator #(.width(3)) comparator_4 (.a(ALUCtl), .b(3'b011), .eq(comparator_4_eq));  // open: gt, lt
  Overflow_Unit overflow_unit_1 (
    .Add(comparator_3_eq), .Sub(comparator_4_eq), .ASign(A[31]), .BSign(B[31]), .ResultSign(ALUResult[31]),
    .Overflow(Overflow));
  not not_1 (Zero, or_2_out);
  or or_2 (or_2_out, ALUResult[0], ALUResult[1], ALUResult[2], ALUResult[3], ALUResult[4], ALUResult[5], ALUResult[6], ALUResult[7], ALUResult[8], ALUResult[9], ALUResult[10], ALUResult[11], ALUResult[12], ALUResult[13], ALUResult[14], ALUResult[15], ALUResult[16], ALUResult[17], ALUResult[18], ALUResult[19], ALUResult[20], ALUResult[21], ALUResult[22], ALUResult[23], ALUResult[24], ALUResult[25], ALUResult[26], ALUResult[27], ALUResult[28], ALUResult[29], ALUResult[30], ALUResult[31]);

  // Other names for the same wires on the sheet: ASign = A[31]; ResultSign = ALUResult[31]; BSign = B[31]

  // Notes on the sheet:
  //   ALUCtl for ADD on top port
  //   ALUCtl for SUB on second port
endmodule

module Register_File (
  input  [4:0] WrAddr,
  input  [31:0] WrData,
  input  WrReg,
  input  [4:0] RdAddr1,
  input  [4:0] RdAddr2,
  input  Clock,
  output [31:0] RdData1,
  output [31:0] RdData2
);

  wire and_1_out, and_2_out, comparator_1_eq, comparator_2_eq, comparator_3_eq, comparator_4_eq, not_1_out,
       not_2_out, WrReg0, WrReg1, WrReg2, WrReg3, WrReg4, WrReg5, WrReg6, WrReg7, WrReg8, WrReg9, WrReg10,
       WrReg11, WrReg12, WrReg13, WrReg14, WrReg15, WrReg16, WrReg17, WrReg18, WrReg19, WrReg20, WrReg21,
       WrReg22, WrReg23, WrReg24, WrReg25, WrReg26, WrReg27, WrReg28, WrReg29, WrReg30, WrReg31;
  wire [31:0] multiplexer_1_out, multiplexer_2_out, RegData1, RegData2, RegData3, RegData4, RegData5,
       RegData6, RegData7, RegData8, RegData9, RegData10, RegData11, RegData12, RegData13, RegData14,
       RegData15, RegData16, RegData17, RegData18, RegData19, RegData20, RegData21, RegData22, RegData23,
       RegData24, RegData25, RegData26, RegData27, RegData28, RegData29, RegData30, RegData31;

  Demultiplexer #(.select(5), .enable("false")) demultiplexer_1 (
    .out0(WrReg0), .out1(WrReg1), .out2(WrReg2), .out3(WrReg3), .out4(WrReg4), .out5(WrReg5), .out6(WrReg6),
    .out7(WrReg7), .out8(WrReg8), .out9(WrReg9), .out10(WrReg10), .out11(WrReg11), .out12(WrReg12),
    .out13(WrReg13), .out14(WrReg14), .out15(WrReg15), .out16(WrReg16), .out17(WrReg17), .out18(WrReg18),
    .out19(WrReg19), .out20(WrReg20), .out21(WrReg21), .out22(WrReg22), .out23(WrReg23), .out24(WrReg24),
    .out25(WrReg25), .out26(WrReg26), .out27(WrReg27), .out28(WrReg28), .out29(WrReg29), .out30(WrReg30),
    .out31(WrReg31), .in(WrReg), .sel(WrAddr));
  // Probe on RegData4
  Register #(.width(32)) Reg4 (.D(WrData), .en(WrReg4), .Q(RegData4), .clk(Clock));  // open: clr
  // Probe on RegData8
  Register #(.width(32)) Reg8 (.D(WrData), .en(WrReg8), .Q(RegData8), .clk(Clock));  // open: clr
  // Probe on RegData12
  Register #(.width(32)) Reg12 (.D(WrData), .en(WrReg12), .Q(RegData12), .clk(Clock));  // open: clr
  // Probe on RegData16
  Register #(.width(32)) Reg16 (.D(WrData), .en(WrReg16), .Q(RegData16), .clk(Clock));  // open: clr
  // Probe on RegData20
  Register #(.width(32)) Reg20 (.D(WrData), .en(WrReg20), .Q(RegData20), .clk(Clock));  // open: clr
  // Probe on RegData24
  Register #(.width(32)) Reg24 (.D(WrData), .en(WrReg24), .Q(RegData24), .clk(Clock));  // open: clr
  // Probe on RegData28
  Register #(.width(32)) Reg28 (.D(WrData), .en(WrReg28), .Q(RegData28), .clk(Clock));  // open: clr
  Register #(.width(32)) Reg1 (.D(WrData), .en(WrReg1), .Q(RegData1), .clk(Clock));  // open: clr
  Register #(.width(32)) Reg5 (.D(WrData), .en(WrReg5), .Q(RegData5), .clk(Clock));  // open: clr
  Register #(.width(32)) Reg9 (.D(WrData), .en(WrReg9), .Q(RegData9), .clk(Clock));  // open: clr
  Register #(.width(32)) Reg13 (.D(WrData), .en(WrReg13), .Q(RegData13), .clk(Clock));  // open: clr
  Register #(.width(32)) Reg17 (.D(WrData), .en(WrReg17), .Q(RegData17), .clk(Clock));  // open: clr
  Register #(.width(32)) Reg21 (.D(WrData), .en(WrReg21), .Q(RegData21), .clk(Clock));  // open: clr
  Register #(.width(32)) Reg25 (.D(WrData), .en(WrReg25), .Q(RegData25), .clk(Clock));  // open: clr
  Register #(.width(32)) Reg29 (.D(WrData), .en(WrReg29), .Q(RegData29), .clk(Clock));  // open: clr
  // Probe on RegData1
  // Probe on RegData5
  // Probe on RegData9
  // Probe on RegData13
  // Probe on RegData17
  // Probe on RegData21
  // Probe on RegData25
  // Probe on RegData29
  // Probe on RegData2
  Register #(.width(32)) Reg2 (.D(WrData), .en(WrReg2), .Q(RegData2), .clk(Clock));  // open: clr
  // Probe on RegData6
  Register #(.width(32)) Reg6 (.D(WrData), .en(WrReg6), .Q(RegData6), .clk(Clock));  // open: clr
  // Probe on RegData10
  Register #(.width(32)) Reg10 (.D(WrData), .en(WrReg10), .Q(RegData10), .clk(Clock));  // open: clr
  // Probe on RegData14
  Register #(.width(32)) Reg14 (.D(WrData), .en(WrReg14), .Q(RegData14), .clk(Clock));  // open: clr
  // Probe on RegData18
  Register #(.width(32)) Reg18 (.D(WrData), .en(WrReg18), .Q(RegData18), .clk(Clock));  // open: clr
  // Probe on RegData22
  Register #(.width(32)) Reg22 (.D(WrData), .en(WrReg22), .Q(RegData22), .clk(Clock));  // open: clr
  // Probe on RegData26
  Register #(.width(32)) Reg26 (.D(WrData), .en(WrReg26), .Q(RegData26), .clk(Clock));  // open: clr
  // Probe on RegData30
  Register #(.width(32)) Reg30 (.D(WrData), .en(WrReg30), .Q(RegData30), .clk(Clock));  // open: clr
  // Probe on RegData3
  Register #(.width(32)) Reg3 (.D(WrData), .en(WrReg3), .Q(RegData3), .clk(Clock));  // open: clr
  // Probe on RegData7
  Register #(.width(32)) Reg7 (.D(WrData), .en(WrReg7), .Q(RegData7), .clk(Clock));  // open: clr
  // Probe on RegData11
  Register #(.width(32)) Reg11 (.D(WrData), .en(WrReg11), .Q(RegData11), .clk(Clock));  // open: clr
  // Probe on RegData15
  Register #(.width(32)) Reg15 (.D(WrData), .en(WrReg15), .Q(RegData15), .clk(Clock));  // open: clr
  // Probe on RegData19
  Register #(.width(32)) Reg19 (.D(WrData), .en(WrReg19), .Q(RegData19), .clk(Clock));  // open: clr
  // Probe on RegData23
  Register #(.width(32)) Reg23 (.D(WrData), .en(WrReg23), .Q(RegData23), .clk(Clock));  // open: clr
  // Probe on RegData27
  Register #(.width(32)) Reg27 (.D(WrData), .en(WrReg27), .Q(RegData27), .clk(Clock));  // open: clr
  // Probe on RegData31
  Register #(.width(32)) Reg31 (.D(WrData), .en(WrReg31), .Q(RegData31), .clk(Clock));  // open: clr
  Multiplexer #(.select(5), .width(32), .enable("false")) multiplexer_1 (
    .in0({32{1'b0}}), .in1(RegData1), .in2(RegData2), .in3(RegData3), .in4(RegData4), .in5(RegData5),
    .in6(RegData6), .in7(RegData7), .in8(RegData8), .in9(RegData9), .in10(RegData10), .in11(RegData11),
    .in12(RegData12), .in13(RegData13), .in14(RegData14), .in15(RegData15), .in16(RegData16),
    .in17(RegData17), .in18(RegData18), .in19(RegData19), .in20(RegData20), .in21(RegData21),
    .in22(RegData22), .in23(RegData23), .in24(RegData24), .in25(RegData25), .in26(RegData26),
    .in27(RegData27), .in28(RegData28), .in29(RegData29), .in30(RegData30), .in31(RegData31),
    .out(multiplexer_1_out), .sel(RdAddr1));
  Multiplexer #(.select(5), .width(32), .enable("false")) multiplexer_2 (
    .in0({32{1'b0}}), .in1(RegData1), .in2(RegData2), .in3(RegData3), .in4(RegData4), .in5(RegData5),
    .in6(RegData6), .in7(RegData7), .in8(RegData8), .in9(RegData9), .in10(RegData10), .in11(RegData11),
    .in12(RegData12), .in13(RegData13), .in14(RegData14), .in15(RegData15), .in16(RegData16),
    .in17(RegData17), .in18(RegData18), .in19(RegData19), .in20(RegData20), .in21(RegData21),
    .in22(RegData22), .in23(RegData23), .in24(RegData24), .in25(RegData25), .in26(RegData26),
    .in27(RegData27), .in28(RegData28), .in29(RegData29), .in30(RegData30), .in31(RegData31),
    .out(multiplexer_2_out), .sel(RdAddr2));
  Multiplexer #(.width(32), .enable("false")) multiplexer_3 (
    .in0(multiplexer_1_out), .in1(WrData), .out(RdData1), .sel(and_1_out));
  Comparator #(.width(5), .mode("unsigned")) comparator_1 (
    .a(WrAddr), .b(RdAddr2), .eq(comparator_1_eq));  // open: gt, lt
  Multiplexer #(.width(32), .enable("false")) multiplexer_4 (
    .in0(multiplexer_2_out), .in1(WrData), .out(RdData2), .sel(and_2_out));
  Comparator #(.width(5), .mode("unsigned")) comparator_2 (
    .a(WrAddr), .b(RdAddr1), .eq(comparator_2_eq));  // open: gt, lt
  and and_1 (and_1_out, comparator_2_eq, WrReg, not_1_out);
  and and_2 (and_2_out, comparator_1_eq, WrReg, not_2_out);
  Comparator #(.width(5), .mode("unsigned")) comparator_3 (
    .a(WrAddr), .b({5{1'b0}}), .eq(comparator_3_eq));  // open: gt, lt
  not not_1 (not_1_out, comparator_3_eq);
  Comparator #(.width(5), .mode("unsigned")) comparator_4 (
    .a(WrAddr), .b({5{1'b0}}), .eq(comparator_4_eq));  // open: gt, lt
  not not_2 (not_2_out, comparator_4_eq);
endmodule

module Overflow_Unit (
  input  Add,
  input  Sub,
  input  ASign,
  input  BSign,
  input  ResultSign,
  output Overflow
);

  wire and_1_out, and_2_out, or_1_out, xnor_1_out, xor_1_out, xor_2_out;

  xnor xnor_1 (xnor_1_out, ASign, BSign);
  xor xor_1 (xor_1_out, ASign, BSign);
  and and_1 (and_1_out, xnor_1_out, Add);
  and and_2 (and_2_out, xor_1_out, Sub);
  or or_1 (or_1_out, and_1_out, and_2_out);
  xor xor_2 (xor_2_out, ResultSign, ASign);
  and and_3 (Overflow, or_1_out, xor_2_out);

  // Notes on the sheet:
  //   Overflow occurs when doing addition and sign(A) == sign(B) && sign(result) != sign(A)
  //   Or
  //   Overflow occurs when doing subtraction and sign(A) != sign(B) && sign(result) != sign(A)
endmodule

module Control_Unit (
  input  [5:0] opcode,
  input  [5:0] func,
  output ALUSrc,
  output Branch,
  output Jal,
  output Jr,
  output Jump,
  output MemRead,
  output MemtoReg,
  output MemWr,
  output RegDst,
  output WrReg,
  output [2:0] ALUCtl
);

  wire comparator_1_eq, comparator_2_eq, isJr;
  wire [2:0] rom_2_data, rom_3_data;
  wire [6:0] rom_1_data;

  Comparator #(.width(6)) comparator_1 (.a(opcode), .b({6{1'b0}}), .eq(comparator_1_eq));  // open: gt, lt
  Comparator #(.width(6)) comparator_2 (.a(6'b001000), .b(func), .eq(comparator_2_eq));  // open: gt, lt
  ROM #(.addrWidth(6), .dataWidth(10)) rom_1 (
    .addr(opcode),
    .data({ALUSrc, Branch, Jal, rom_1_data[6], Jump, MemRead, MemtoReg, MemWr, rom_1_data[1:0]}));  // open: sel
  and and_1 (isJr, comparator_1_eq, comparator_2_eq);
  ROM #(.addrWidth(6), .dataWidth(3)) rom_2 (.addr(opcode), .data(rom_2_data));  // open: sel
  ROM #(.addrWidth(6), .dataWidth(3)) rom_3 (.addr(func), .data(rom_3_data));  // open: sel
  Multiplexer #(.enable("false")) multiplexer_1 (.in0(rom_1_data[6]), .in1(1'b1), .out(Jr), .sel(isJr));
  Multiplexer #(.enable("false")) multiplexer_2 (.in0(rom_1_data[1]), .in1(1'b0), .out(RegDst), .sel(isJr));
  Multiplexer #(.enable("false")) multiplexer_3 (.in0(rom_1_data[0]), .in1(1'b0), .out(WrReg), .sel(isJr));
  Multiplexer #(.width(3), .enable("false")) multiplexer_4 (
    .in0(rom_2_data), .in1(rom_3_data), .out(ALUCtl), .sel(comparator_1_eq));

  // Notes on the sheet:
  //   contents of rom_1 (hex, n*v repeats v):
  //   3 0 20 a1 100 0 0 0 201 0 0 0 201 201 21*0 219 7*0 204
  //   contents of rom_2 (hex, n*v repeats v):
  //   4*0 3 0 0 0 1 4*0 2 21*0 1 7*0 1
  //   contents of rom_3 (hex, n*v repeats v):
  //   8*0 1 23*0 1 0 3 0 0 2 5 0 0 0 4
endmodule

module IF_ID (
  input  Clock,
  input  [31:0] in_2,
  input  [31:0] in_3,
  output [31:0] out_4,
  output [31:0] out_5
);

  Register #(.width(32)) register_1 (.D(in_2), .Q(out_4), .clk(Clock));  // open: en, clr
  Register #(.width(32)) register_2 (.D(in_3), .Q(out_5), .clk(Clock));  // open: en, clr

  // Other names for the same wires on the sheet: Reg_Instr_Mem[31:0] = out_5; Reg_PC_4[31:0] = out_4
endmodule

module ID_EX (
  input  Clock,
  input  in_2,
  input  in_3,
  input  in_4,
  input  in_5,
  input  in_6,
  input  [1:0] in_7,
  input  in_8,
  input  in_9,
  input  [31:0] in_10,
  input  [31:0] in_11,
  input  [31:0] in_12,
  input  [31:0] in_13,
  output out_14,
  output out_15,
  output out_16,
  output out_17,
  output out_18,
  output [1:0] out_19,
  output out_20,
  output out_21,
  output [31:0] out_22,
  output [31:0] out_23,
  output [31:0] out_24,
  output [31:0] out_25
);

  Register #(.width(32)) register_1 (.D(in_10), .Q(out_22), .clk(Clock));  // open: en, clr
  Register #(.width(32)) register_2 (.D(in_11), .Q(out_23), .clk(Clock));  // open: en, clr
  Register #(.width(32)) register_3 (.D(in_12), .Q(out_24), .clk(Clock));  // open: en, clr
  Register #(.width(32)) register_4 (.D(in_13), .Q(out_25), .clk(Clock));  // open: en, clr
  Register #(.width(1)) register_5 (.D(in_2), .Q(out_14), .clk(Clock));  // open: en, clr
  Register #(.width(1)) register_6 (.D(in_3), .Q(out_15), .clk(Clock));  // open: en, clr
  Register #(.width(1)) register_7 (.D(in_4), .Q(out_16), .clk(Clock));  // open: en, clr
  Register #(.width(1)) register_8 (.D(in_5), .Q(out_17), .clk(Clock));  // open: en, clr
  Register #(.width(1)) register_9 (.D(in_6), .Q(out_18), .clk(Clock));  // open: en, clr
  Register #(.width(2)) register_10 (.D(in_7), .Q(out_19), .clk(Clock));  // open: en, clr
  Register #(.width(1)) register_11 (.D(in_8), .Q(out_20), .clk(Clock));  // open: en, clr
  Register #(.width(1)) register_12 (.D(in_9), .Q(out_21), .clk(Clock));  // open: en, clr

  // Other names for the same wires on the sheet: ALUOp[1:0] = in_7; ALUSrc = in_8; Branch = in_9;
  //   Reg_ALUOp[1:0] = out_19; Reg_ALUSrc = out_20; Reg_Branch = out_21; Reg_MemRead = out_16; Reg_MemtoReg = out_15;
  //   Reg_MemWrite = out_17; Reg_PC_4[31:0] = out_22; Reg_Rd_Data_1[31:0] = out_23; Reg_Rd_Data_2[31:0] = out_24;
  //   Reg_RegDst = out_18; Reg_RegWrite = out_14; Reg_Sign_Extended[31:0] = out_25; RegDst = in_6

  // Notes on the sheet:
  //   WB
  //   M
  //   Ex
endmodule

module EX_MEM (
  input  Clock,
  input  in_2,
  input  in_3,
  input  in_4,
  input  in_5,
  input  in_6,
  input  [31:0] in_7,
  input  Zero,
  input  [31:0] in_9,
  input  [31:0] in_10,
  output out_11,
  output out_12,
  output out_13,
  output out_14,
  output out_15,
  output [31:0] out_16,
  output out_17,
  output [31:0] out_18,
  output [31:0] out_19
);

  wire Reg_Zero_t;

  Register #(.width(32)) register_1 (.D(in_7), .Q(out_16), .clk(Clock));  // open: en, clr
  Register #(.width(32)) register_2 (.D(in_10), .Q(out_19), .clk(Clock));  // open: en, clr
  Register #(.width(1)) register_3 (.D(in_2), .Q(out_11), .clk(Clock));  // open: en, clr
  Register #(.width(1)) register_4 (.D(in_3), .Q(out_12), .clk(Clock));  // open: en, clr
  Register #(.width(1)) register_5 (.D(in_4), .Q(out_13), .clk(Clock));  // open: en, clr
  Register #(.width(1)) register_6 (.D(in_5), .Q(out_14), .clk(Clock));  // open: en, clr
  Register #(.width(1)) register_7 (.D(in_6), .Q(out_15), .clk(Clock));  // open: en, clr
  Register #(.width(1)) register_8 (.D(Zero), .Q(Reg_Zero_t), .clk(Clock));  // open: en, clr
  Register #(.width(32)) register_9 (.D(in_9), .Q(out_18), .clk(Clock));  // open: en, clr

  // Other names for the same wires on the sheet: ALU_Result[31:0] = in_9; Reg_Adder[31:0] = out_16;
  //   Reg_ALU_Result[31:0] = out_18; Reg_Branch = out_11; Reg_MemRead = out_14; Reg_MemtoReg = out_13;
  //   Reg_MemWrite = out_15; Reg_Rd_Data_2[31:0] = out_19; Reg_RegWrite = out_12; Reg_Zero = out_17

  // Notes on the sheet:
  //   M
endmodule

module MEM_WB (
  input  Clock,
  input  in_2,
  input  in_3,
  input  [31:0] in_4,
  input  [31:0] in_5,
  output out_6,
  output out_7,
  output [31:0] out_8,
  output [31:0] out_9
);

  Register #(.width(32)) register_1 (.D(in_4), .Q(out_8), .clk(Clock));  // open: en, clr
  Register #(.width(32)) register_2 (.D(in_5), .Q(out_9), .clk(Clock));  // open: en, clr
  Register #(.width(1)) register_3 (.D(in_2), .Q(out_6), .clk(Clock));  // open: en, clr
  Register #(.width(1)) register_4 (.D(in_3), .Q(out_7), .clk(Clock));  // open: en, clr

  // Other names for the same wires on the sheet: Reg_ALU_Result[31:0] = out_9; Reg_MemtoReg = out_7;
  //   Reg_Rd_Data[31:0] = out_8; Reg_RegWrite = out_6

  // Notes on the sheet:
  //   WB
endmodule
